# Fritzing sketch LEDs_PushButton (saved by Fritzing 0.9.3b)
breadboards: 1

parts:
  U2 = NodeMCU V1.0
  LED7 = LED - 5mm [color="Red (633nm)" package="5 mm [THT]"]
  LED8 = LED - 5mm [color="Red (633nm)" package="5 mm [THT]"]
  LED9 = LED - 5mm [color="Red (633nm)" package="5 mm [THT]"]
  LED11 = LED - 5mm [color="Red (633nm)" package="5 mm [THT]"]
  S1 = Pushbutton [package="[THT]"]
  R1 = Resistor [tolerance=±5% resistance=220 package=THT]
  LED12 = LED - 5mm [color="Red (633nm)" package="5 mm [THT]"]
  LED10 = LED - 5mm [color="Red (633nm)" package="5 mm [THT]"]

nets:
  N1: U2.D0, LED11.anode
  N2: U2.D1, LED10.anode
  N3: U2.D3, LED9.anode
  N4: U2.3V3, S1.Pin_1, S1.Pin_2
  N5: U2.GND, LED7.cathode, LED8.cathode, LED9.cathode, LED11.cathode, R1.Pin_0, LED12.cathode, LED10.cathode
  N6: U2.D5, LED8.anode
  N7: U2.D6, S1.Pin_3, S1.Pin_4, R1.Pin_1
  N8: U2.D7, LED12.anode
  N9: U2.D8, LED7.anode

custom parts:
  NodeMCU V1.0: ESP8266 based NodeMCU
